# Fritzing sketch Branchement_arduino_mega (saved by Fritzing 0.9.3b)
circuit board: 9.17004cm x 5.6607cm

parts:
  Composant1 = Arduino Mega 2560 (Rev3)
  J3 = shrouded pin header, 16 pins [form="♂ (shrouded male)"]
  WeMos_D1_Mini1 = WeMos D1 Mini
  Composant2 = Real Time Clock Module - DS1307 RTC Breakout Board

nets:
  N1: Composant1.A0, J3.pin4
  N2: Composant1.A1, J3.pin13
  N3: Composant1.A2, J3.pin3
  N4: Composant1.A3, J3.pin14
  N5: Composant1.D21/SCL, Composant1.SCL, Composant2.SCL
  N6: Composant1.D20/SDA, Composant1.SDA, Composant2.SDA
  N7: Composant1.D19/RX1, WeMos_D1_Mini1.TX
  GND: Composant1.GND, J3.pin10, J3.pin12, J3.pin16, WeMos_D1_Mini1.G, Composant2.GND
  N8: Composant1.D11_PWM, J3.pin2
  N9: Composant1.D10_PWM, J3.pin15
  N10: Composant1.D9_PWM, J3.pin1
  3V3: Composant1.3V3, Composant2.5V
  5V: Composant1.5V, WeMos_D1_Mini1.5V
  N11: Composant1.D24, J3.pin8
  N12: Composant1.D25, J3.pin9
  N13: Composant1.D26, J3.pin7
  N14: Composant1.D27, J3.pin6
  N15: Composant1.D28, J3.pin11
  N16: Composant1.D29, J3.pin5
